# Fritzing sketch kula (saved by Fritzing 0.8.5b)
circuit board: 8.46667cm x 5.64444cm
breadboards: 1

parts:
  IC1 = MAX1044 [chip_label=IC package="DIP (Dual Inline) [THT]"]
  J1 = Power Jack [package=power_jack_slot]
  C1 = Electrolytic Capacitor [capacitance=10µF package="100 mil [THT, electrolytic]"]
  C2 = Electrolytic Capacitor [capacitance=10µF package="100 mil [THT, electrolytic]"]
  IC2 = Voltage Regulator [package=to220-igo]
  C3 = Electrolytic Capacitor [capacitance=0.47mF package="100 mil [THT, electrolytic]"]
  C4 = Ceramic Capacitor [capacitance=10nF package="100 mil [THT, multilayer]"]
  C5 = Ceramic Capacitor [capacitance=10nF package="100 mil [THT, multilayer]"]
  Atmega1 = ATmega644 [package=pdpi]
  XTAL1 = Crystal [frequency="16 Mhz" package=THT]
  C11 = Ceramic Capacitor [capacitance=10pF package="100 mil [THT, multilayer]"]
  C12 = Ceramic Capacitor [capacitance=10pF package="100 mil [THT, multilayer]"]
  JP1 = Header 5x2 [package=2x5-ra]
  LED1 = LED - 5mm [color="Red (633nm)" package="5 mm [THT]"]
  R1 = Resistor [tolerance=±5% resistance=220 package=THT]
  R2 = Resistor [tolerance=±5% resistance=47k package=THT]
  JP2 = Header 3 [package=screwterminal-3.5mm-3_lock.007s]
  U1 = POT [package=pot_alpha_rv16af-20]
  S1 = Pushbutton [package="[THT]"]
  IC3 = 6N137 [chip_label=IC package="DIP (Dual Inline) [THT]"]
  DIN1 = DIN-5 jack (MIDI) [package=THT]
  R3 = Resistor [tolerance=±5% resistance=220 package=THT]
  R4 = Resistor [tolerance=±5% resistance=6.8k package=THT]
  R5 = Resistor [tolerance=±5% resistance=1.5k package=THT]
  DIN2 = DIN-5 jack (MIDI) [package=THT]
  R6 = Resistor [tolerance=±5% resistance=220 package=THT]
  R7 = Resistor [tolerance=±5% resistance=220 package=THT]

nets:
  9V: IC1.BOOST, IC1.V+, J1.PWR, IC2.IN, C3.+, C4.1
  N1: IC1.CAP+, C1.+
  GND: IC1.GND, J1.GND, C2.-, IC2.GND, C3.-, C4.0, C5.0, Atmega1.GND, C11.1, C12.1, JP1.4, JP1.6, JP1.8, JP1.10, R1.Pin_1, JP2.1, U1.A, S1.Pin_2, IC3.pin5, R4.Pin_0
  N2: IC1.CAP-, C1.-
  -9V: IC1.Vout, C2.+
  5V: IC2.OUT, C5.1, Atmega1.VCC, Atmega1.AVCC, Atmega1.AREF, JP1.2, R2.Pin_0, U1.E, IC3.pin8, R5.Pin_0, R6.Pin_0
  N3: Atmega1.PB5, JP1.1
  N4: Atmega1.PB6, JP1.9
  N5: Atmega1.PB7, JP1.7
  N6: Atmega1.RESET, JP1.5, R2.Pin_1
  N7: Atmega1.XTAL2, XTAL1.pin_0, C11.0
  N8: Atmega1.XTAL1, XTAL1.pin_1, C12.0
  N9: Atmega1.PD0, JP2.2, IC3.pin6, R5.Pin_1
  N10: Atmega1.PD1, JP2.3, R7.Pin_0
  N11: Atmega1.PC0, LED1.anode
  N12: Atmega1.PA1, S1.Pin_4
  N13: Atmega1.PA0, U1.S
  N14: LED1.cathode, R1.Pin_0
  N15: IC3.pin2, R3.Pin_0
  N16: IC3.pin3, DIN1.4
  N17: IC3.pin7, R4.Pin_1
  N18: DIN1.5, R3.Pin_1
  N19: DIN2.5, R6.Pin_1
  N20: DIN2.4, R7.Pin_1

notes:
  6N137
  [MAX 1044
  7805

custom parts:
  MAX1044: Max 1044
  6N137: A DIP stand-in part for whatever IC you want. With 8 pins on a 300mil dual inline package (DIP) footprint.
