# Fritzing sketch kula_voice_section (saved by Fritzing 0.8.5b)
breadboards: 1

parts:
  IC1 = IC, DIP package, 14 pins [chip_label=4024]
  J1 = female pin header, 11 pins [form="♀ (female)"]
  IC2 = IC, DIP package, 14 pins [chip_label=4024]
  IC3 = IC, DIP package, 14 pins [chip_label=4024]
  IC4 = IC, DIP package, 14 pins [chip_label=4024]
  IC5 = IC, DIP package, 14 pins [chip_label=4024]
  IC6 = IC, DIP package, 14 pins [chip_label=4024]
  R1 = Resistor [tolerance=±5% resistance=220 package=THT]
  R2 = Resistor [tolerance=±5% resistance=220 package=THT]
  R3 = Resistor [tolerance=±5% resistance=220 package=THT]
  R4 = Resistor [tolerance=±5% resistance=220 package=THT]
  R5 = Resistor [tolerance=±5% resistance=220 package=THT]
  R6 = Resistor [tolerance=±5% resistance=220 package=THT]
  R7 = Resistor [tolerance=±5% resistance=220 package=THT]
  R8 = Resistor [tolerance=±5% resistance=220 package=THT]
  R9 = Resistor [tolerance=±5% resistance=220 package=THT]
  R10 = Resistor [tolerance=±5% resistance=220 package=THT]
  R11 = Resistor [tolerance=±5% resistance=220 package=THT]
  R12 = Resistor [tolerance=±5% resistance=220 package=THT]
  R13 = Resistor [tolerance=±5% resistance=220 package=THT]
  R14 = Resistor [tolerance=±5% resistance=220 package=THT]
  R15 = Resistor [tolerance=±5% resistance=220 package=THT]
  R16 = Resistor [tolerance=±5% resistance=220 package=THT]
  R17 = Resistor [tolerance=±5% resistance=220 package=THT]
  R18 = Resistor [tolerance=±5% resistance=220 package=THT]
  R19 = Resistor [tolerance=±5% resistance=220 package=THT]
  R20 = Resistor [tolerance=±5% resistance=220 package=THT]
  R21 = Resistor [tolerance=±5% resistance=220 package=THT]
  R22 = Resistor [tolerance=±5% resistance=220 package=THT]
  R23 = Resistor [tolerance=±5% resistance=220 package=THT]
  R24 = Resistor [tolerance=±5% resistance=220 package=THT]
  LF1 = LF444 [chip_label=LF444 package="DIP (Dual Inline) [THT]"]
  C1 = Electrolytic Capacitor [capacitance=1µF package="100 mil [THT, electrolytic]"]
  C2 = Electrolytic Capacitor [capacitance=1µF package="100 mil [THT, electrolytic]"]
  C3 = Electrolytic Capacitor [capacitance=1µF package="100 mil [THT, electrolytic]"]
  C4 = Electrolytic Capacitor [capacitance=1µF package="100 mil [THT, electrolytic]"]
  C5 = Electrolytic Capacitor [capacitance=1µF package="100 mil [THT, electrolytic]"]
  C6 = Electrolytic Capacitor [capacitance=1µF package="100 mil [THT, electrolytic]"]
  C7 = Electrolytic Capacitor [capacitance=1µF package="100 mil [THT, electrolytic]"]
  C8 = Electrolytic Capacitor [capacitance=1µF package="100 mil [THT, electrolytic]"]
  C9 = Electrolytic Capacitor [capacitance=1µF package="100 mil [THT, electrolytic]"]
  C10 = Electrolytic Capacitor [capacitance=1µF package="100 mil [THT, electrolytic]"]
  C11 = Electrolytic Capacitor [capacitance=1µF package="100 mil [THT, electrolytic]"]
  C12 = Electrolytic Capacitor [capacitance=1µF package="100 mil [THT, electrolytic]"]
  C13 = Electrolytic Capacitor [capacitance=1µF package="100 mil [THT, electrolytic]"]
  C14 = Electrolytic Capacitor [capacitance=1µF package="100 mil [THT, electrolytic]"]
  C15 = Electrolytic Capacitor [capacitance=1µF package="100 mil [THT, electrolytic]"]
  C16 = Electrolytic Capacitor [capacitance=1µF package="100 mil [THT, electrolytic]"]
  C17 = Electrolytic Capacitor [capacitance=1µF package="100 mil [THT, electrolytic]"]
  C18 = Electrolytic Capacitor [capacitance=1µF package="100 mil [THT, electrolytic]"]
  C19 = Electrolytic Capacitor [capacitance=1µF package="100 mil [THT, electrolytic]"]
  C20 = Electrolytic Capacitor [capacitance=1µF package="100 mil [THT, electrolytic]"]
  C21 = Electrolytic Capacitor [capacitance=1µF package="100 mil [THT, electrolytic]"]
  C22 = Electrolytic Capacitor [capacitance=1µF package="100 mil [THT, electrolytic]"]
  C23 = Electrolytic Capacitor [capacitance=1µF package="100 mil [THT, electrolytic]"]
  C24 = Electrolytic Capacitor [capacitance=1µF package="100 mil [THT, electrolytic]"]
  R25 = Resistor [tolerance=±5% resistance=220 package=THT]
  R26 = Resistor [tolerance=±5% resistance=220 package=THT]
  R27 = Resistor [tolerance=±5% resistance=220 package=THT]
  R28 = Resistor [tolerance=±5% resistance=220 package=THT]
  LF2 = LF442 [chip_label=LF442 package="DIP (Dual Inline) [THT]"]
  R29 = Resistor [tolerance=±5% resistance=220 package=THT]
  R30 = Resistor [tolerance=±5% resistance=220 package=THT]
  R31 = Resistor [tolerance=±5% resistance=220 package=THT]
  R32 = Resistor [tolerance=±5% resistance=220 package=THT]
  R33 = Resistor [tolerance=±5% resistance=220 package=THT]
  R34 = Resistor [tolerance=±5% resistance=220 package=THT]

nets:
  N1: IC1.pin1, J1.pin3, C6.+
  N2: IC1.pin2, IC1.pin7, J1.pin2, IC2.pin2, IC2.pin7, IC3.pin2, IC3.pin7, IC4.pin2, IC4.pin7, IC5.pin2, IC5.pin7, IC6.pin2, IC6.pin7, LF1.pin3, LF1.pin5, LF1.pin10, LF1.pin12, LF2.pin3
  N3: IC1.pin9, C9.+
  N4: IC1.pin11, C8.+
  N5: IC1.pin12, C7.+
  N6: IC1.pin14, J1.pin1, IC2.pin14, IC3.pin14, IC4.pin14, IC5.pin14, IC6.pin14
  N7: J1.pin4, IC2.pin1, C5.+
  N8: J1.pin5, IC3.pin1, C4.+
  N9: J1.pin6, IC5.pin1, C3.+
  N10: J1.pin7, IC6.pin1, C2.+
  N11: J1.pin8, IC4.pin1, C1.+
  N12: J1.pin9, R29.Pin_0
  N13: J1.pin10, LF1.pin4, LF2.pin8
  N14: J1.pin11, LF1.pin11, LF2.pin4
  N15: IC2.pin9, C12.+
  N16: IC2.pin11, C11.+
  N17: IC2.pin12, C10.+
  N18: IC3.pin9, C15.+
  N19: IC3.pin11, C14.+
  N20: IC3.pin12, C13.+
  N21: IC4.pin9, C24.+
  N22: IC4.pin11, C23.+
  N23: IC4.pin12, C22.+
  N24: IC5.pin9, C18.+
  N25: IC5.pin11, C17.+
  N26: IC5.pin12, C16.+
  N27: IC6.pin9, C21.+
  N28: IC6.pin11, C20.+
  N29: IC6.pin12, C19.+
  N30: R1.Pin_0, R2.Pin_0, R3.Pin_0, R4.Pin_0, R5.Pin_0, R6.Pin_0, LF1.pin2, R25.Pin_0
  N31: R1.Pin_1, C3.-
  N32: R2.Pin_1, C4.-
  N33: R3.Pin_1, C5.-
  N34: R4.Pin_1, C2.-
  N35: R5.Pin_1, C6.-
  N36: R6.Pin_1, C1.-
  N37: R7.Pin_0, R8.Pin_0, R9.Pin_0, R10.Pin_0, R11.Pin_0, R12.Pin_0, LF1.pin6, R26.Pin_0
  N38: R7.Pin_1, C13.-
  N39: R8.Pin_1, C19.-
  N40: R9.Pin_1, C22.-
  N41: R10.Pin_1, C7.-
  N42: R11.Pin_1, C10.-
  N43: R12.Pin_1, C16.-
  N44: R13.Pin_0, R14.Pin_0, R15.Pin_0, R16.Pin_0, R17.Pin_0, R18.Pin_0, LF1.pin13, R27.Pin_1
  N45: R13.Pin_1, C23.-
  N46: R14.Pin_1, C14.-
  N47: R15.Pin_1, C11.-
  N48: R16.Pin_1, C8.-
  N49: R17.Pin_1, C17.-
  N50: R18.Pin_1, C20.-
  N51: R19.Pin_0, R20.Pin_0, R21.Pin_0, R22.Pin_0, R23.Pin_0, R24.Pin_0, LF1.pin9, R28.Pin_1
  N52: R19.Pin_1, C24.-
  N53: R20.Pin_1, C15.-
  N54: R21.Pin_1, C12.-
  N55: R22.Pin_1, C9.-
  N56: R23.Pin_1, C18.-
  N57: R24.Pin_1, C21.-
  N58: LF1.pin1, R25.Pin_1, R30.Pin_0
  N59: LF1.pin7, R26.Pin_1, R33.Pin_0
  N60: LF1.pin8, R28.Pin_0, R32.Pin_0
  N61: LF1.pin14, R27.Pin_0, R31.Pin_0
  N62: LF2.pin1, R34.Pin_1
  N63: LF2.pin2, R29.Pin_1, R30.Pin_1, R31.Pin_1, R32.Pin_1, R33.Pin_1, R34.Pin_0

notes:
  5V
  GND
  OSC1
  OSC2
  OSC3
  OSC4
  OSC5
  OSC6
  NOISE
  V+
  V-

custom parts:
  LF444: A DIP stand-in part for whatever IC you want. With 14 pins on a 300mil dual inline package (DIP) footprint.
